// Logisim project ALU.circ as structural Verilog: 4 circuits, main circuit ALU
module ALU (
  input  [7:0] A,
  input  [7:0] B,
  input  [2:0] F2F1F0,
  output Z,
  output [7:0] Output,
  output N,
  output Cout
);

  wire cell_1_cout, cell_2_cout, cell_3_cout, cell_4_cout, cell_5_cout, cell_6_cout, cell_7_cout,
       multiplexer_1_out;

  \cell  cell_1 (
    .A(A[0]), .B(B[0]), .Cin(multiplexer_1_out), .Cout(cell_1_cout), .C(Output[0]), .F0(F2F1F0[0]),
    .F1(F2F1F0[1]), .F2(F2F1F0[2]));
  Multiplexer #(.select(3), .enable("false")) multiplexer_1 (
    .in0(1'b0), .in1(1'b0), .in2(1'b1), .in3(1'b1), .in4(1'b0), .in5(1'b1), .in6(1'b0), .in7(1'b0),
    .out(multiplexer_1_out), .sel(F2F1F0));
  \cell  cell_2 (
    .A(A[1]), .B(B[1]), .Cin(cell_1_cout), .Cout(cell_2_cout), .C(Output[1]), .F0(F2F1F0[0]), .F1(F2F1F0[1]),
    .F2(F2F1F0[2]));
  \cell  cell_3 (
    .A(A[2]), .B(B[2]), .Cin(cell_2_cout), .Cout(cell_3_cout), .C(Output[2]), .F0(F2F1F0[0]), .F1(F2F1F0[1]),
    .F2(F2F1F0[2]));
  \cell  cell_4 (
    .A(A[3]), .B(B[3]), .Cin(cell_3_cout), .Cout(cell_4_cout), .C(Output[3]), .F0(F2F1F0[0]), .F1(F2F1F0[1]),
    .F2(F2F1F0[2]));
  \cell  cell_5 (
    .A(A[4]), .B(B[4]), .Cin(cell_4_cout), .Cout(cell_5_cout), .C(Output[4]), .F0(F2F1F0[0]), .F1(F2F1F0[1]),
    .F2(F2F1F0[2]));
  \cell  cell_6 (
    .A(A[5]), .B(B[5]), .Cin(cell_5_cout), .Cout(cell_6_cout), .C(Output[5]), .F0(F2F1F0[0]), .F1(F2F1F0[1]),
    .F2(F2F1F0[2]));
  \cell  cell_7 (
    .A(A[6]), .B(B[6]), .Cin(cell_6_cout), .Cout(cell_7_cout), .C(Output[6]), .F0(F2F1F0[0]), .F1(F2F1F0[1]),
    .F2(F2F1F0[2]));
  \cell  cell_8 (
    .A(A[7]), .B(B[7]), .Cin(cell_7_cout), .Cout(Cout), .C(N), .F0(F2F1F0[0]), .F1(F2F1F0[1]), .F2(F2F1F0[2]));
  nor nor_1 (Z, Output[0], Output[1], Output[2], Output[3], Output[4], Output[5], Output[6], N);

  assign Output[7] = N;

  // Notes on the sheet:
  //   +1 when substracting or adding 1
  //   Function selector
  //   A
  //   B
  //   8 bit ALU with 8 different operations
  //   Operations: A, B, A+1, B+1, A+B, A-B, A and B, A or B
  //   Output
endmodule

module adder (
  input  A,
  input  B,
  input  Cin,
  output S,
  output Cout
);

  wire and_1_out, and_2_out, xor_1_out;

  xor xor_1 (xor_1_out, A, B);
  xor xor_2 (S, xor_1_out, Cin);
  and and_1 (and_1_out, xor_1_out, Cin);
  and and_2 (and_2_out, A, B);
  or or_1 (Cout, and_1_out, and_2_out);
endmodule

module addersubstractor (
  input  A,
  input  B,
  input  Cin,
  input  Substract,
  output S,
  output Cout
);

  wire multiplexer_1_out, not_1_out;

  Multiplexer #(.enable("false")) multiplexer_1 (.in0(B), .in1(not_1_out), .out(multiplexer_1_out), .sel(Substract));
  not not_1 (not_1_out, B);
  adder adder_1 (.A(A), .B(multiplexer_1_out), .Cin(Cin), .S(S), .Cout(Cout));
endmodule

module \cell  (
  input  A,
  input  B,
  input  Cin,
  input  F0,
  input  F1,
  input  F2,
  output Cout,
  output C
);

  wire addersubstractor_1_s, and_1_out, and_2_out, and_3_out, and_4_out, multiplexer_1_out,
       multiplexer_2_out, not_1_out, not_2_out, not_3_out, not_4_out, or_1_out;

  Multiplexer #(.enable("false")) multiplexer_1 (.in0(A), .in1(1'b0), .out(multiplexer_1_out), .sel(and_2_out));
  Multiplexer #(.enable("false")) multiplexer_2 (.in0(B), .in1(1'b0), .out(multiplexer_2_out), .sel(and_1_out));
  and and_1 (and_1_out, not_1_out, F1, not_2_out);
  and and_2 (and_2_out, F0, F1, not_3_out);
  and and_3 (and_3_out, F0, not_4_out, F2);
  addersubstractor addersubstractor_1 (
    .A(multiplexer_1_out), .B(multiplexer_2_out), .Cin(Cin), .Substract(and_3_out), .S(addersubstractor_1_s),
    .Cout(Cout));
  not not_1 (not_1_out, F0);
  not not_2 (not_2_out, F2);
  not not_3 (not_3_out, F2);
  not not_4 (not_4_out, F1);
  and and_4 (and_4_out, multiplexer_1_out, multiplexer_2_out);
  or or_1 (or_1_out, multiplexer_1_out, multiplexer_2_out);
  Multiplexer #(.select(3), .enable("false")) multiplexer_3 (
    .in0(multiplexer_1_out), .in1(multiplexer_2_out), .in2(addersubstractor_1_s), .in3(addersubstractor_1_s),
    .in4(addersubstractor_1_s), .in5(addersubstractor_1_s), .in6(and_4_out), .in7(or_1_out), .out(C),
    .sel({F2, F1, F0}));

  // Notes on the sheet:
  //   010 = A+1
  //   011 => B+1
  //   101 => A-B
  //   Single Cell Of ALU
  //   Implemented:
  //   for functions
  //   A, B, A+B, A-B, A and B, A or B, A+1, B+1
  //   See http://i.imgur.com/1lqP8gA.png
endmodule
