// Logisim project CPU.circ as structural Verilog: 3 circuits, main circuit CPU
module CPU (
  input  [7:0] Data,
  input  Clock,
  input  [7:0] ExtInput,
  output [7:0] Address,
  output [7:0] Output
);

  wire ctrl0, ctrl1, ctrl2, ctrl3, ctrl4, stackEn, stackFunc;
  wire [1:0] alu_1_n, MIR_q, Status;
  wire [2:0] ALU, JPMC;
  wire [5:0] jam_unit_1_mpc_out, MIR, MPC_q, multiplexer_1_out;
  wire [7:0] A_q, alu_1_output, B_q, main_1_dataout, MBR, multiplexer_2_out;
  wire [23:0] MicroprogramStorage_data;
  wire [23:21] MIR_q_2;

  Register u_MBR (.D(Data), .en(ctrl4), .clk(Clock), .Q(MBR));  // open: clr
  Multiplexer #(.width(6), .enable("false")) multiplexer_1 (
    .in0(MIR), .in1(MBR[5:0]), .out(multiplexer_1_out), .sel(JPMC[2]));
  Register PC (.D(main_1_dataout), .en(ctrl3), .clk(Clock), .Q(Address));  // open: clr
  JAM_Unit jam_unit_1 (.ZN_in(Status), .MPC_in(multiplexer_1_out), .MPC_out(jam_unit_1_mpc_out), .JAMZ_N(JPMC[1:0]));
  Register Out (.D(main_1_dataout), .en(ctrl2), .clk(Clock), .Q(Output));  // open: clr
  Register #(.width(6)) MPC (.D(jam_unit_1_mpc_out), .en(1'b1), .clk(Clock), .Q(MPC_q));  // open: clr
  ROM #(.addrWidth(6), .dataWidth(24)) MicroprogramStorage (.addr(MPC_q), .data(MicroprogramStorage_data));
  Register B (.D(main_1_dataout), .en(ctrl1), .clk(Clock), .Q(B_q));  // open: clr
  Register A (.D(main_1_dataout), .en(ctrl0), .clk(Clock), .Q(A_q));  // open: clr
  Multiplexer #(.select(2), .width(8), .enable("false")) multiplexer_2 (
    .in0(B_q), .in1(MBR), .in2(Address), .in3(ExtInput), .out(multiplexer_2_out), .sel(MIR_q));
  Register #(.width(24), .trigger("falling")) u_MIR (
    .D(MicroprogramStorage_data), .en(1'b1), .clk(Clock),
    .Q({MIR_q_2, stackFunc, stackEn, MIR, JPMC, ALU, ctrl4, ctrl3, ctrl2, ctrl1, ctrl0, MIR_q}));  // open: clr
  stacken_main main_1 (
    .DataIn(alu_1_output), .clk(Clock), .PushPop(stackFunc), .Enable(stackEn), .DataOut(main_1_dataout));
  ALU alu_1 (
    .A(A_q), .B(multiplexer_2_out), .F2F1F0(ALU), .Output(alu_1_output), .N(alu_1_n[0]), .Z(alu_1_n[1]));  // open: Cout
  Register #(.width(2)) StatusReg (.D(alu_1_n), .en(1'b1), .clk(Clock), .Q(Status));  // open: clr

  // Other names for the same wires on the sheet: clk = Clock

  // Notes on the sheet:
  //   contents of MicroprogramStorage (hex, n*v repeats v):
  //   2040 4182 61a2 1000 0 c083 87 10000 10 104 a1 180c1 1a085 1c182 1a2 12100 0 24000 8 28280 284 2c200
  //   204 30280 1aa80 34000 1a800 38280 1a680 140c1 0 3e000 42000 180000 46000 80004
  //   Bselect
  //   Stack
endmodule

module Test_Cpu (
  input  [7:0] Input,
  output [7:0] out_2,
  output [7:0] Output
);

  wire clock_1_out;
  wire [7:0] cpu_1_address;

  ROM rom_1 (.addr(cpu_1_address), .data(out_2));
  CPU cpu_1 (.Data(out_2), .ExtInput(Input), .Output(Output), .Address(cpu_1_address), .Clock(clock_1_out));
  Clock clock_1 (.out(clock_1_out));

  // Notes on the sheet:
  //   contents of rom_1 (hex, n*v repeats v):
  //   b 0 7 f 1d 2
  //   Program memory
  //   Data (goes to MBR)
endmodule

module JAM_Unit (
  input  [1:0] ZN_in,
  input  [5:0] MPC_in,
  input  [1:0] JAMZ_N,
  output [5:0] MPC_out
);

  wire multiplexer_1_out, multiplexer_2_out, or_1_out;

  or or_1 (or_1_out, multiplexer_1_out, multiplexer_2_out);
  Multiplexer #(.enable("false")) multiplexer_1 (.in0(1'b0), .in1(ZN_in[0]), .out(multiplexer_1_out), .sel(JAMZ_N[0]));
  Multiplexer #(.enable("false")) multiplexer_2 (.in0(1'b0), .in1(ZN_in[1]), .out(multiplexer_2_out), .sel(JAMZ_N[1]));
  or or_2 (MPC_out[4], or_1_out, MPC_in[4]);

  assign {MPC_out[5], MPC_out[3:0]} = {MPC_in[5], MPC_in[3:0]};

  // Notes on the sheet:
  //   Quick and dirty OR-ing of the MSB of the address
endmodule
