// Logisim project CPU_backup.circ as structural Verilog: 2 circuits, main circuit Test_Cpu
module CPU (
  input  [7:0] Data,
  input  Clock,
  input  [7:0] ExtInput,
  output [7:0] Address,
  output [1:0] out_5,
  output [7:0] Output
);

  wire ctrl0, ctrl1, ctrl2, ctrl3, ctrl4, JPMC;
  wire [1:0] nor_1_out;
  wire [2:0] ALU;
  wire [4:0] MPC_q, multiplexer_1_out;
  wire [7:0] A_q, alu_1_p4, B_q, MBR, multiplexer_2_out;
  wire [15:0] MicroprogramStorage_data, MIR;

  Register u_MBR (.D(Data), .en(ctrl4), .clk(Clock), .Q(MBR));  // open: clr
  Register PC (.D(alu_1_p4), .en(ctrl3), .clk(Clock), .Q(Address));  // open: clr
  Multiplexer #(.width(5), .enable("false")) multiplexer_1 (
    .in0(MIR[15:11]), .in1(MBR[4:0]), .out(multiplexer_1_out), .sel(JPMC));
  Register Out (.D(alu_1_p4), .en(ctrl2), .clk(Clock), .Q(Output));  // open: clr
  Register #(.width(5)) MPC (.D(multiplexer_1_out), .en(1'b1), .clk(Clock), .Q(MPC_q));  // open: clr
  ROM #(.addrWidth(5), .dataWidth(16)) MicroprogramStorage (.addr(MPC_q), .data(MicroprogramStorage_data));
  Register B (.D(alu_1_p4), .en(ctrl1), .clk(Clock), .Q(B_q));  // open: clr
  Register A (.D(alu_1_p4), .en(ctrl0), .clk(Clock), .Q(A_q));  // open: clr
  Multiplexer #(.select(2), .width(8), .enable("false")) multiplexer_2 (
    .in0(B_q), .in1(MBR), .in2(Address), .in3(ExtInput), .out(multiplexer_2_out), .sel(MIR[1:0]));
  Register #(.width(16), .trigger("falling")) u_MIR (
    .D(MicroprogramStorage_data), .en(1'b1), .clk(Clock),
    .Q({MIR[15:11], JPMC, ALU, ctrl4, ctrl3, ctrl2, ctrl1, ctrl0, MIR[1:0]}));  // open: clr
  // ALU alu_1: pin names not known; wires that end beside it: A_q, multiplexer_2_out, ALU, alu_1_p4, nor_1_out[1]
  nor nor_1 (nor_1_out[0], alu_1_p4[0], alu_1_p4[1], alu_1_p4[2], alu_1_p4[3], alu_1_p4[4], alu_1_p4[5], alu_1_p4[6], alu_1_p4[7]);
  Register #(.width(2)) StatusReg (.D(nor_1_out), .en(1'b1), .clk(Clock), .Q(out_5));  // open: clr

  // Other names for the same wires on the sheet: clk = Clock;
  //   MIR[10:2] = {JPMC, ALU, ctrl4, ctrl3, ctrl2, ctrl1, ctrl0}; Status[1:0] = out_5

  // Notes on the sheet:
  //   External Memory Data Bus
  //   contents of MicroprogramStorage (hex, n*v repeats v):
  //   840 1182 19a2 400 0 3083 87 4000 10 50c1 a1 60c1 6885 7182 1a2 8100 104 9000 9808 a280 284 b200 204
  //   8*0 f800
  //   Bselect
endmodule

module Test_Cpu (
  input  [7:0] in_1,
  output [7:0] out_2,
  output [7:0] out_3
);

  wire clock_1_out;
  wire [7:0] cpu_1_address;

  ROM rom_1 (.addr(cpu_1_address), .data(out_2));
  CPU cpu_1 (
    .Data(out_2), .ExtInput(in_1), .Output(out_3), .Address(cpu_1_address), .Clock(clock_1_out));  // open: out_5
  Clock clock_1 (.out(clock_1_out));

  // Notes on the sheet:
  //   contents of rom_1 (hex, n*v repeats v):
  //   b 5 11 b 9 13 7
endmodule
