// Logisim project stacken.circ as structural Verilog: 1 circuit, main circuit main
module main (
  input  [7:0] DataIn,
  input  clk,
  input  PushPop,
  input  Enable,
  output [7:0] DataOut
);

  wire clk_t, M1, M2, not_1_out, not_2_out, not_3_out;
  wire [3:0] counter_1_q;

  not not_1 (not_1_out, PushPop);
  assign clk_t = not_1_out ? ~clk : 1'bz;  // Controlled_Inverter controlled_inverter_1
  assign clk_t = PushPop ? clk : 1'bz;  // Controlled_Buffer controlled_buffer_1
  Counter #(.width(4), .max('hf), .trigger("falling")) counter_1 (
    .load(1'b0), .up(PushPop), .count(Enable), .clk(clk_t), .Q(counter_1_q));  // open: clr, D, carry
  not not_2 (not_2_out, PushPop);
  and and_1 (M1, PushPop, Enable);
  and and_2 (M2, Enable, not_2_out);
  not not_3 (not_3_out, M2);
  RAM #(.addrWidth(4)) ram_1 (.addr(counter_1_q), .we(M1), .oe(M2), .clk(clk_t), .data(DataOut));
  assign DataOut = not_3_out ? DataIn : 8'bz;  // Controlled_Buffer controlled_buffer_2

  // Other names for the same wires on the sheet: UpDown = PushPop
endmodule
